# Fritzing sketch Schematics (saved by Fritzing 0.9.3b)

parts:
  MKRFox2 = Arduino MKR Fox 1200
  KY-008_Laserdiode3 = Laser [part_number=1219301 package=keys]
  R1 = Photocell (LDR) [package=THT]
  R2 = Resistor [tolerance=±5% resistance=10k package=THT]

nets:
  N1: MKRFox2.A1, R2.Pin_1
  N2: MKRFox2.1, KY-008_Laserdiode3.connector1pin
  N3: MKRFox2.GND, R2.Pin_0
  N4: MKRFox2.VCC, KY-008_Laserdiode3.connector0pin, R1.pin_1
  N5: KY-008_Laserdiode3.connector2pin, R1.pin_0

custom parts:
  Laser: KEYES KY-008 650nm Laser Transmitter Module
